// Logisim project comparador_igualdade.circ as structural Verilog: 1 circuit, main circuit main
module main (
  input  [3:0] A,
  input  [3:0] B,
  output \Saída 
);

  wire xor_1_out, xor_2_out, xor_3_out, xor_4_out;

  xor xor_1 (xor_1_out, B[0], A[0]);
  xor xor_2 (xor_2_out, B[1], A[1]);
  xor xor_3 (xor_3_out, B[2], A[2]);
  xor xor_4 (xor_4_out, B[3], A[3]);
  nor nor_1 (\Saída , xor_1_out, xor_2_out, xor_3_out, xor_4_out);
endmodule
