// Logisim project comparador_menorque.circ as structural Verilog: 1 circuit, main circuit main
module main (
  input  [3:0] A,
  input  [3:0] B,
  output \Saída 
);

  wire and_1_out, and_2_out, and_3_out, and_4_out, xnor_1_out, xnor_2_out, xnor_3_out;

  and and_1 (and_1_out, B[3], ~A[3]);  // AND_Gate
  xnor xnor_1 (xnor_1_out, A[3], B[3]);
  and and_2 (and_2_out, xnor_1_out, B[2], ~A[2]);  // AND_Gate
  xnor xnor_2 (xnor_2_out, B[2], A[2]);
  and and_3 (and_3_out, xnor_2_out, B[1], ~A[1]);  // AND_Gate
  xnor xnor_3 (xnor_3_out, B[1], A[1]);
  and and_4 (and_4_out, xnor_3_out, B[0], ~A[0]);  // AND_Gate
  or or_1 (\Saída , and_1_out, and_2_out, and_3_out, and_4_out);
endmodule
