// Logisim project somador.circ as structural Verilog
module hallfAdder (
  input  in_1,
  input  in_2,
  output out_3,
  output out_4
);

  xor xor_1 (out_3, in_1, in_2);
  and and_1 (out_4, in_1, in_2);
endmodule

module somador1bit (
  input  CARRY_IN,
  input  CARRY_IN_2,
  input  A,
  input  A_2,
  input  B,
  input  B_2,
  output OUT,
  output OUT_2,
  output CARRY_OUT,
  output CARRY_OUT_2
);

  wire and_1_out, and_2_out, hallfadder_1_out_3, hallfadder_1_out_4, hallfadder_2_out_4, xor_1_out;

  and and_1 (and_1_out, B_2, A_2);
  xor xor_1 (xor_1_out, A_2, B_2);
  and and_2 (and_2_out, xor_1_out, CARRY_IN);
  or or_1 (CARRY_OUT_2, and_1_out, and_2_out);
  xor xor_2 (OUT_2, CARRY_IN, xor_1_out);
  hallfAdder hallfadder_1 (.in_1(A), .in_2(B), .out_3(hallfadder_1_out_3), .out_4(hallfadder_1_out_4));
  hallfAdder hallfadder_2 (.in_1(hallfadder_1_out_3), .in_2(CARRY_IN_2), .out_3(OUT), .out_4(hallfadder_2_out_4));
  or or_2 (CARRY_OUT, hallfadder_1_out_4, hallfadder_2_out_4);
endmodule
