// Logisim project subtrator.circ as structural Verilog: 1 circuit, main circuit subtrator
module subtrator (
  input  A,
  input  B,
  input  Emprestado,
  output Saida,
  output SAIDA_EMPRESTADO
);

  wire and_1_out, and_2_out, and_3_out, xor_1_out;

  xor xor_1 (xor_1_out, A, B);
  and and_1 (and_1_out, ~A, Emprestado);  // AND_Gate
  and and_2 (and_2_out, ~A, B);  // AND_Gate
  and and_3 (and_3_out, B, Emprestado);
  xor xor_2 (Saida, xor_1_out, Emprestado);
  or or_1 (SAIDA_EMPRESTADO, and_1_out, and_2_out, and_3_out);
endmodule
